# Fritzing sketch weather_clock (saved by Fritzing 0.9.2b)
breadboards: 1

parts:
  Part1 = Photon
  VCC1 = 4 x AAA Battery Mount
  J1 = Basic Servo
  Q1 = NPN-Transistor [package="TO92 [THT]"]
  R1 = Resistor [tolerance=±5% resistance=220 package=THT]

nets:
  N1: Part1.GND, VCC1.-, Q1.E
  VIN: Part1.VIN, VCC1.+, J1.vcc
  N2: Part1.D0, J1.pulse
  N3: Part1.D1, R1.Pin_1
  N4: J1.gnd, Q1.C
  N5: Q1.B, R1.Pin_0
